# Fritzing sketch circuit (saved by Fritzing 0.9.4)
stripboards: 8

parts:
  U1 = Battery Holders [package=battery-aa]
  U2 = Battery Holders [package=battery-aa]
  U3 = Battery Holders [package=battery-aa]
  U4 = Battery Holders [package=battery-aa]
  Mod1 = 2S-BMS
  A1 = cks pd65W
  U5 = LM2596 step down module
  F1 = FUSE [package=fuse_5mm]
  F2 = FUSE [package=fuse_5mm]
  F3 = FUSE [package=fuse_5mm]
  F4 = FUSE [package=fuse_5mm]
  S1 = SWITCH-MOMENTARY-2 [package=tactile-switch-1101ne]
  U6 = LM2596 step down module
  U7 = LM2596 step down module
  A2 = Littlebee 20A ESC
  Raspberry_Pi_1 = Raspberry Pi 3 [part_number=RPI-3-V1.2]
  IC1 = Rasberry Pi NIOR Camera [chip_label=IC package="DIP (Dual Inline) [THT]"]  # not connected
  부품1 = Adafruit PCA9685 PWM/Servo Breakout [part_number=815]
  J1 = Basic Servo
  M1 = DC Motor
  M2 = DC Motor
  C1 = Capacitor Polarized [package=cpol-radial-1000uf-25v]
  LED2 = smd LED [color="Red (633nm)" package="0603 [SMD]"]
  LED3 = smd LED [color="Blue (430nm)" package="0603 [SMD]"]
  LED4 = smd LED [color="Green (555nm)" package="0603 [SMD]"]

nets:
  N1: U1.-, U2.-, U3.+, U4.+, Mod1.pin3#4
  N2: U1.+, U2.+, Mod1.pin1
  N3: U3.-, U4.-, Mod1.pin2
  GND: Mod1.pin3#2, A1.Pin_2, U5.IN-, U5.OUT-, U6.IN-, U6.OUT-, U7.IN-, U7.OUT-, A2.Pin_1, A2.Pin_3, Raspberry_Pi_1.GND, 부품1.GND, J1.gnd, M1.pin_2, M2.pin_2, C1.-, LED2.cathode, LED3.cathode
  N4: Mod1.pin3#3, F1.2, F4.1
  N5: A1.Pin_1, U5.IN+
  N6: U5.OUT+, F1.1
  N7: F2.1, U6.IN+
  N8: F2.2, F3.2, S1.1, A2.Pin_2, LED2.anode
  N9: F3.1, U7.IN+
  N10: F4.2, S1.2
  N11: U6.OUT+, LED4.anode
  N12: U7.OUT+, 부품1.5.0V, J1.vcc, C1.+, LED3.anode
  N13: A2.Pin_5, 부품1.PWM0
  3V3: Raspberry_Pi_1.3v3, Raspberry_Pi_1.3V3, 부품1.VCC
  N14: Raspberry_Pi_1.GPIO2, 부품1.SDA
  N15: Raspberry_Pi_1.GPIO3, 부품1.SCL
  N16: Raspberry_Pi_1.5V, M1.pin_1, M2.pin_1
  N17: 부품1.PWM14, J1.pulse

custom parts:
  2S-BMS: 2S-BMS LIPO battery charger / protection unit. Note pcb does not match the board as it will likely connect with wires, so pcb is 5 pads suitable for .1in header pins.
  cks pd65W: QC4.0 QC3.0 Type-C USB PD65W Fast Charging Adapter Module DC8-32V 3.25A 65W Step Down Module For Huawei SCP/FCP Apple PD.
  LM2596 step down module: LM2596 DC-DC step down power supply module 3 A.
  Littlebee 20A ESC: LittleBee 20A 2-4 LiPo Battery OPTO ESC Brushless Speed Controller for RC FPV Multicopter.
  Rasberry Pi NIOR Camera: Camera
  Adafruit PCA9685 PWM/Servo Breakout: Using only two pins, control 16 free-running PWM outputs! I2C-controlled PWM driver with a built in clock. Unlike the TLC5940 family, you do not need to continuously send it signal tying up your microcontroller, its completely free running! 5V compliant, which means you can control it from a 3.3V microcontroller and still safely drive up to 6V outputs (this is good for when you want to control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
